# Fritzing sketch cicuitDiagramEditable (saved by Fritzing 0.9.3b)
circuit board: 8.46667cm x 5.64444cm
breadboards: 1

parts:
  Part1 = Arduino Mega 2560 (Rev3)
  X1 = DC Motor
  X2 = DC Motor
  X3 = DC Motor
  Z1 = DC Motor
  Y3 = DC Motor
  Z2 = DC Motor
  Y2 = DC Motor
  Y1 = DC Motor
  Z3 = DC Motor
  Z4 = DC Motor
  X = H-Bridge [package=THT]
  Z1-2 = H-Bridge [package=THT]
  Z3-4 = H-Bridge [package=THT]
  VCC1 = Battery block 9V
  VCC5 = Battery block 9V
  VCC6 = Battery block 9V
  VCC7 = Battery
  VCC8 = Battery block 9V
  VCC9 = Battery block 9V
  C7 = Electrolytic Capacitor [package="100 mil [THT, electrolytic]"]
  C8 = Electrolytic Capacitor [package="100 mil [THT, electrolytic]"]
  VCC10 = Battery block 9V
  VCC11 = Battery block 9V
  VCC12 = Battery block 9V
  C9 = Electrolytic Capacitor [package="100 mil [THT, electrolytic]"]
  VCC13 = Battery block 9V
  C10 = Electrolytic Capacitor [package="100 mil [THT, electrolytic]"]
  RGBLEDOnLCD = RGB LED (com. cathode, rgb) [package="5 mm [THT]"]
  R2 = Resistor [tolerance=±5% resistance=330 package=THT]
  LED3 = Super Flux LED blue [color=Blue]
  Part2 = Bluetooth Mate Silver
  R3 = Resistor [tolerance=±5% resistance=330 package=THT]
  Vibe1 = Vibration Motor- ROB-08449 [package=vibe-motor-10mm]
  Vibe2 = Vibration Motor- ROB-08449 [package=vibe-motor-10mm]
  Vibe3 = Vibration Motor- ROB-08449 [package=vibe-motor-10mm]
  Vibe14 = Vibration Motor- ROB-08449 [package=vibe-motor-10mm]
  Vibe13 = Vibration Motor- ROB-08449 [package=vibe-motor-10mm]
  Vibe12 = Vibration Motor- ROB-08449 [package=vibe-motor-10mm]
  Vibe11 = Vibration Motor- ROB-08449 [package=vibe-motor-10mm]
  Vibe10 = Vibration Motor- ROB-08449 [package=vibe-motor-10mm]
  Vibe9 = Vibration Motor- ROB-08449 [package=vibe-motor-10mm]
  Vibe8 = Vibration Motor- ROB-08449 [package=vibe-motor-10mm]
  Vibe7 = Vibration Motor- ROB-08449 [package=vibe-motor-10mm]
  Vibe6 = Vibration Motor- ROB-08449 [package=vibe-motor-10mm]
  Vibe5 = Vibration Motor- ROB-08449 [package=vibe-motor-10mm]
  Vibe4 = Vibration Motor- ROB-08449 [package=vibe-motor-10mm]
  Vibe16 = Vibration Motor- ROB-08449 [package=vibe-motor-10mm]
  Vibe15 = Vibration Motor- ROB-08449 [package=vibe-motor-10mm]
  Rotary = Rotary Potentiometer (Small) [maximum_resistance=100kΩ package=THT]
  Slider = Slide Potentiometer [maximum_resistance=100kΩ]
  S1 = Pushbutton [package="[THT]"]
  ShiftReg1-DIP = 74HC595 SMD [package="SO16 [SMD]"]
  ShiftReg2-DIP = 74HC595 [package="DIP16 [THT]"]
  VCC4 = Battery block 9V
  ShiftReg3 = 74HC595 [package="DIP16 [THT]"]
  Q1 = NPN-Transistor [package="TO92 [THT]"]
  Q5 = NPN-Transistor [package="TO92 [THT]"]
  Q7 = NPN-Transistor [package="TO92 [THT]"]
  Q8 = NPN-Transistor [package="TO92 [THT]"]
  Q9 = NPN-Transistor [package="TO92 [THT]"]
  Q10 = NPN-Transistor [package="TO92 [THT]"]
  R4 = Resistor [tolerance=±5% resistance=1k package=THT]
  R8 = Resistor [tolerance=±5% resistance=1k package=THT]
  R10 = Resistor [tolerance=±5% resistance=1k package=THT]
  R11 = Resistor [tolerance=±5% resistance=1k package=THT]
  R12 = Resistor [tolerance=±5% resistance=1k package=THT]
  R13 = Resistor [tolerance=±5% resistance=1k package=THT]
  LED4 = LED - 5mm [color="Green (570nm)" package="5 mm [THT]"]
  R15 = Resistor [tolerance=±5% resistance=220 package=THT]
  LED5 = LED - 5mm [color="Green (570nm)" package="5 mm [THT]"]
  R16 = Resistor [tolerance=±5% resistance=220 package=THT]
  LED6 = LED - 5mm [color="Green (570nm)" package="5 mm [THT]"]
  R17 = Resistor [tolerance=±5% resistance=220 package=THT]
  LED7 = LED - 5mm [color="Green (570nm)" package="5 mm [THT]"]
  R18 = Resistor [tolerance=±5% resistance=220 package=THT]
  LED8 = LED - 5mm [color="Green (570nm)" package="5 mm [THT]"]
  R19 = Resistor [tolerance=±5% resistance=220 package=THT]
  LED9 = LED - 5mm [color="Green (570nm)" package="5 mm [THT]"]
  R20 = Resistor [tolerance=±5% resistance=220 package=THT]
  LED10 = LED - 5mm [color="Green (570nm)" package="5 mm [THT]"]
  R21 = Resistor [tolerance=±5% resistance=220 package=THT]
  LED11 = LED - 5mm [color="Green (570nm)" package="5 mm [THT]"]
  R22 = Resistor [tolerance=±5% resistance=220 package=THT]
  LED12 = LED - 5mm [color="Green (570nm)" package="5 mm [THT]"]
  R23 = Resistor [tolerance=±5% resistance=220 package=THT]
  LED13 = LED - 5mm [color="Green (570nm)" package="5 mm [THT]"]
  R24 = Resistor [tolerance=±5% resistance=220 package=THT]
  Part3 = Real Time Clock Module - DS1307 RTC Breakout Board
  pull-up1 = Resistor [tolerance=±5% resistance=220 package=THT]
  pull-up1_2 = Resistor [tolerance=±5% resistance=220 package=THT]
  Y = H-Bridge [package=THT]
  S2 = Pushbutton [package="[THT]"]
  R25 = Resistor [tolerance=±5% resistance=10k package=THT]
  R26 = Resistor [tolerance=±5% resistance=10k package=THT]

nets:
  N1: Part1.A14, Rotary.wiper
  N2: Part1.A15, Slider.wiper
  N3: Part1.D15/RX3, Part2.TX_5V
  N4: Part1.D14/TX3, Part2.RX_5V
  GND: Part1.GND, X.GND1, X.GND2, X.GND3, X.GND4, Z1-2.GND1, Z1-2.GND2, Z1-2.GND3, Z1-2.GND4, Z3-4.GND1, Z3-4.GND2, Z3-4.GND3, Z3-4.GND4, VCC1.-, VCC5.-, VCC6.-, VCC7.-, VCC8.-, VCC9.-, C7.-, C8.-, VCC10.-, VCC11.-, VCC12.-, C9.-, VCC13.-, C10.-, R2.Pin_0, Part2.GND, R3.Pin_0, Vibe1.-, Vibe2.-, Vibe3.-, Vibe14.-, Vibe13.-, Vibe12.-, Vibe11.-, Vibe10.-, Vibe9.-, Vibe8.-, Vibe7.-, Vibe6.-, Vibe5.-, Vibe4.-, Vibe16.-, Vibe15.-, Rotary.leg1, Slider.leg1, ShiftReg1-DIP.GND, ShiftReg2-DIP.GND, VCC4.-, ShiftReg3.GND, ShiftReg3.OE, Q1.E, Q5.E, Q7.E, Q8.E, Q9.E, Q10.E, Part3.GND, Y.GND1, Y.GND2, Y.GND3, Y.GND4, R25.Pin_1, R26.Pin_1
  N5: Part1.D11_PWM, Z3-4.3_4EN
  N6: Part1.D10_PWM, Z3-4.1_2EN
  N7: Part1.D9_PWM, Z1-2.3_4EN
  N8: Part1.D8_PWM, Z1-2.1_2EN
  N9: Part1.IOREF, Part2.VCC, Rotary.leg2, Slider.leg2
  VCC: Part1.5V, X.VCC1, S1.Pin_3, S1.Pin_4, ShiftReg1-DIP.MR, ShiftReg1-DIP.VCC, ShiftReg2-DIP.MR, ShiftReg2-DIP.VCC, ShiftReg3.MR, ShiftReg3.VCC, Part3.5V, pull-up1.Pin_1, Y.VCC1, S2.Pin_1, S2.Pin_2
  N10: Part1.VIN, VCC4.+
  N11: Part1.D2_PWM, X.1_2EN
  N12: Part1.D4_PWM, Y.1_2EN
  N13: Part1.D5_PWM, RGBLEDOnLCD.green_anode
  N14: Part1.D6_PWM, RGBLEDOnLCD.blue_anode
  N15: Part1.D7_PWM, RGBLEDOnLCD.red_anode
  N16: Part1.D22, X.1A
  N17: Part1.D23, X.2A
  N18: Part1.D24, S2.Pin_3, S2.Pin_4, R26.Pin_0
  N19: Part1.D26, Y.1A
  N20: Part1.D27, Y.2A
  N21: Part1.D34, Z1-2.1A
  N22: Part1.D35, Z1-2.2A
  N23: Part1.D36, Z1-2.4A
  N24: Part1.D37, Z1-2.3A
  N25: Part1.D38, Z3-4.1A
  N26: Part1.D39, Z3-4.2A
  N27: Part1.D40, Z3-4.4A
  N28: Part1.D41, Z3-4.3A
  N29: Part1.D42, LED3.cathode
  N30: Part1.D43, ShiftReg3.DS
  N31: Part1.D44, ShiftReg3.ST_CP
  N32: Part1.D45, ShiftReg3.SH_CP
  N33: Part1.D49, ShiftReg1-DIP.OE, ShiftReg2-DIP.OE
  N34: Part1.D50, S1.Pin_1, R25.Pin_0
  N35: Part1.D51, ShiftReg1-DIP.DS
  N36: Part1.D52, ShiftReg1-DIP.ST_CP, ShiftReg2-DIP.ST_CP
  N37: Part1.D53, ShiftReg1-DIP.SH_CP, ShiftReg2-DIP.SH_CP
  N38: X1.pin_1, X2.pin_1, X3.pin_1, X.1Y
  N39: X1.pin_2, X2.pin_2, X3.pin_2, X.2Y
  N40: Z1.pin_1, Z1-2.1Y
  N41: Z1.pin_2, Z1-2.2Y
  N42: Y3.pin_1, Y2.pin_1, Y1.pin_1, Y.1Y
  N43: Y3.pin_2, Y2.pin_2, Y1.pin_2, Y.2Y
  N44: Z2.pin_1, Z1-2.4Y
  N45: Z2.pin_2, Z1-2.3Y
  N46: Z3.pin_1, Z3-4.1Y
  N47: Z3.pin_2, Z3-4.2Y
  N48: Z4.pin_1, Z3-4.4Y
  N49: Z4.pin_2, Z3-4.3Y
  N50: X.VCC2, VCC1.+, VCC5.+, VCC6.+, LED4.anode, LED5.anode, LED6.anode
  N51: Z1-2.VCC2, C7.+, VCC10.+, LED10.anode
  N52: Z1-2.VCC1, C8.+, VCC11.+, LED11.anode
  N53: Z3-4.VCC2, VCC12.+, C9.+, LED12.anode
  N54: Z3-4.VCC1, VCC13.+, C10.+, LED13.anode
  N55: VCC7.+, VCC8.+, VCC9.+, LED7.anode, LED8.anode, LED9.anode, Y.VCC2
  N56: RGBLEDOnLCD.common_cathode, R2.Pin_1
  N57: LED3.anode, R3.Pin_1
  N58: Vibe1.+, ShiftReg1-DIP.Q0
  N59: Vibe2.+, ShiftReg1-DIP.Q1
  N60: Vibe3.+, ShiftReg1-DIP.Q2
  N61: Vibe14.+, ShiftReg2-DIP.Q5
  N62: Vibe13.+, ShiftReg2-DIP.Q4
  N63: Vibe12.+, ShiftReg2-DIP.Q3
  N64: Vibe11.+, ShiftReg2-DIP.Q2
  N65: Vibe10.+, ShiftReg2-DIP.Q1
  N66: Vibe9.+, ShiftReg2-DIP.Q0
  N67: Vibe8.+, ShiftReg1-DIP.Q7
  N68: Vibe7.+, ShiftReg1-DIP.Q6
  N69: Vibe6.+, ShiftReg1-DIP.Q5
  N70: Vibe5.+, ShiftReg1-DIP.Q4
  N71: Vibe4.+, ShiftReg1-DIP.Q3
  N72: Vibe16.+, ShiftReg2-DIP.Q7
  N73: Vibe15.+, ShiftReg2-DIP.Q6
  N74: ShiftReg1-DIP.Q7', ShiftReg2-DIP.DS
  N75: ShiftReg3.Q1, R8.Pin_0
  N76: ShiftReg3.Q2, R10.Pin_1
  N77: ShiftReg3.Q3, R11.Pin_1
  N78: ShiftReg3.Q4, R12.Pin_1
  N79: ShiftReg3.Q0, R4.Pin_0
  N80: Q1.B, R4.Pin_1
  N81: Q1.C, R15.Pin_1, R16.Pin_0, R17.Pin_0
  N82: Q5.B, R8.Pin_1
  N83: Q5.C, R18.Pin_0, R19.Pin_0, R20.Pin_1
  N84: Q7.B, R10.Pin_0
  N85: Q7.C, R21.Pin_0
  N86: Q8.B, R11.Pin_0
  N87: Q8.C, R22.Pin_0
  N88: Q9.B, R12.Pin_0
  N89: Q9.C, R23.Pin_0
  N90: Q10.B, R13.Pin_0
  N91: Q10.C, R24.Pin_0
  N92: LED4.cathode, R15.Pin_0
  N93: LED5.cathode, R16.Pin_1
  N94: LED6.cathode, R17.Pin_1
  N95: LED7.cathode, R18.Pin_1
  N96: LED8.cathode, R19.Pin_1
  N97: LED9.cathode, R20.Pin_0
  N98: LED10.cathode, R21.Pin_1
  N99: LED11.cathode, R22.Pin_1
  N100: LED12.cathode, R23.Pin_1
  N101: LED13.cathode, R24.Pin_1
  N102: Part3.SCL, pull-up1_2.Pin_0
  N103: Part3.SDA, pull-up1.Pin_0

custom parts:
  Electrolytic Capacitor: A small electrolytic capacitor
